# Fritzing sketch Handshake (saved by Fritzing 0.9.4)
circuit board: 7cm x 5cm
breadboards: 2

parts:
  U1 = LuaNode32 / ESP32 [part_number=ESP32S-PIN30]
  J1 = Basic Servo
  J2 = Basic Servo
  U2 = SBX DSUN [package=THT]
  +9v- = Battery block 9V
  J3 = male pin header, 4 pins [form="♂ (male)"]

nets:
  GND: U1.GND, J1.gnd, J2.gnd, U2.GND, +9v-.-, J3.pin3
  VCC: U1.Vin, J1.vcc, J2.vcc, U2.+VOUT
  N1: U1.3V3, J3.pin4
  N2: U1.D19, J3.pin2
  N3: U1.D21, J3.pin1
  N4: U1.D22, J1.pulse
  N5: U1.D23, J2.pulse
  N6: U2.+VIN, +9v-.+

custom parts:
  LuaNode32 / ESP32: New Image for LuaNode32 DOIT ESP32 DEVKIT V1. Base parts from LuaNode32 / ESP32 ESP32 based LuaNode32 by G.Noorlander DOIT Esp32 DevKit v1 (30 pins long, 11 pins width) by Werner Rothschopf (modified by vanepp Dec 2018)
  SBX DSUN: SBX DSUN input voltage 4.5 - 28V DC output voltage .8v to 20VDC (step down converter) Output current 3A max
